// Logisim project imm-gen.circ as structural Verilog: 1 circuit, main circuit imm_gen
module imm_gen (
  input  [31:0] Instruction,
  input  [2:0] ImmSel,
  output [31:0] Immediate
);

  wire [31:11] ImmI, ImmS;
  wire [31:12] ImmB;
  wire [31:20] ImmJ;

  assign ImmI = {{20{Instruction[31]}}, Instruction[31]};  // Bit_Extender bit_extender_1
  assign ImmS = {{20{Instruction[31]}}, Instruction[31]};  // Bit_Extender bit_extender_2
  assign ImmB = {{19{Instruction[31]}}, Instruction[31]};  // Bit_Extender bit_extender_3
  assign ImmJ = {{11{Instruction[31]}}, Instruction[31]};  // Bit_Extender bit_extender_4
  Multiplexer #(.select(3), .width(32)) multiplexer_1 (
    .in0({ImmI, Instruction[30:20]}), .in1({ImmS, Instruction[30:25], Instruction[11:7]}),
    .in2({ImmB, Instruction[7], Instruction[30:25], Instruction[11:8], 1'b0}),
    .in3({Instruction[31:12], {12{1'b0}}}),
    .in4({ImmJ, Instruction[19:12], Instruction[20], Instruction[30:21], 1'b0}), .out(Immediate), .sel(ImmSel));  // open: in5, in6, in7

  // Other names for the same wires on the sheet: ImmB[11:1] = {Instruction[7], Instruction[30:25], Instruction[11:8]};
  //   ImmS[10:0] = {Instruction[30:25], Instruction[11:7]}; ImmI[10:0] = Instruction[30:20];
  //   ImmJ[19:1] = {Instruction[19:12], Instruction[20], Instruction[30:21]}; ImmU[31:12] = Instruction[31:12]

  // Notes on the sheet:
  //   INPUTS to your circuit
  //   DON'T CHANGE THE LOCATIONS OF THE INPUTS AND OUTPUTS!
  //   OUTPUT from your circuit
endmodule
