// Logisim project partial-store.circ as structural Verilog: 1 circuit, main circuit partial_store
module partial_store (
  input  [31:0] Instruction,
  input  [31:0] MemAddress,
  input  [31:0] DataFromReg,
  input  MemWEn,
  output [3:0] MemWriteMask,
  output [31:0] DataToMem
);

  wire comparator_1_eq, write;
  wire [3:0] maskb, maskh, multiplexer_4_out;
  wire [7:0] undriven, undriven_2, undriven_3, undriven_4, undriven_5, undriven_6, undriven_7, undriven_8,
       undriven_9, undriven_12, undriven_13, undriven_14;
  wire [15:0] undriven_10, undriven_11;
  wire [31:0] multiplexer_7_out, wrb, wrh;

  Multiplexer #(.select(2), .width(4)) multiplexer_1 (
    .in0(4'b0001), .in1(4'b0010), .in2(4'b0100), .in3(4'b1000), .out(maskb), .sel(MemAddress[1:0]));
  Multiplexer #(.select(2), .width(4)) multiplexer_2 (
    .in0(4'b0011), .in2(4'b1100), .out(maskh), .sel(MemAddress[1:0]));  // open: in1, in3
  Multiplexer #(.width(4)) multiplexer_3 (.in0(4'b0000), .in1(multiplexer_4_out), .out(MemWriteMask), .sel(write));
  Multiplexer #(.select(3), .width(4)) multiplexer_4 (
    .in0(maskb), .in1(maskh), .in2(4'b1111), .out(multiplexer_4_out), .sel(Instruction[14:12]));  // open: in3, in4, in5, in6, in7
  Comparator #(.width(7)) comparator_1 (.a(Instruction[6:0]), .b(7'b0100011), .eq(comparator_1_eq));  // open: gt, lt
  and and_1 (write, MemWEn, comparator_1_eq);
  Multiplexer #(.select(2), .width(32)) multiplexer_5 (
    .in0({undriven_3, undriven_2, undriven, DataFromReg[7:0]}),
    .in1({undriven_6, undriven_5, DataFromReg[7:0], undriven_4}),
    .in2({undriven_9, DataFromReg[7:0], undriven_8, undriven_7}),
    .in3({DataFromReg[7:0], undriven_14, undriven_13, undriven_12}), .out(wrb), .sel(MemAddress[1:0]));
  Multiplexer #(.select(2), .width(32)) multiplexer_6 (
    .in0({undriven_10, DataFromReg[15:0]}), .in2({DataFromReg[15:0], undriven_11}), .out(wrh),
    .sel(MemAddress[1:0]));  // open: in1, in3
  Multiplexer #(.select(3), .width(32)) multiplexer_7 (
    .in0(wrb), .in1(wrh), .in2(DataFromReg), .out(multiplexer_7_out), .sel(Instruction[14:12]));  // open: in3, in4, in5, in6, in7
  Multiplexer #(.width(32)) multiplexer_8 (.in0({32{1'b0}}), .in1(multiplexer_7_out), .out(DataToMem), .sel(write));

  // Other names for the same wires on the sheet: data8[7:0] = DataFromReg[7:0]; data16[15:0] = DataFromReg[15:0];
  //   wrw[31:0] = DataFromReg; opcode[6:0] = Instruction[6:0]; func3[2:0] = Instruction[14:12];
  //   bt2[1:0] = MemAddress[1:0]

  // Notes on the sheet:
  //   INPUTS to your circuit
  //   DON'T CHANGE THE LOCATIONS OF THE INPUTS AND OUTPUTS!
  //   OUTPUT from your circuit
endmodule
