// Logisim project regfile.circ as structural Verilog: 1 circuit, main circuit regfile
module regfile (
  input  [4:0] ReadIndex1,
  input  [4:0] ReadIndex2,
  input  [4:0] WriteIndex,
  input  [31:0] WriteData,
  input  RegWEn,
  input  clk,
  output [31:0] ra,
  output [31:0] sp,
  output [31:0] t0,
  output [31:0] t1,
  output [31:0] t2,
  output [31:0] s0,
  output [31:0] s1,
  output [31:0] a0,
  output [31:0] ReadData1,
  output [31:0] ReadData2
);

  wire r1, r2, r3, r4, r5, r6, r7, r8, r9, r10, r11, r12, r13, r14, r15, r16, r17, r18, r19, r20, r21, r22,
       r23, r24, r25, r26, r27, r28, r29, r30, r31, r32;
  wire [31:0] o1, o4, o5, o12, o13, o14, o15, o16, o17, o18, o19, o20, o21, o22, o23, o24, o25, o26, o27,
       o28, o29, o30, o31, o32, Write1;

  Register #(.width(32)) register_1 (.D(Write1), .en(1'b0), .clk(clk), .Q(o1));  // open: clr
  Register #(.width(32)) register_2 (.D(WriteData), .en(r5), .clk(clk), .Q(o5));  // open: clr
  Register #(.width(32)) register_3 (.D(WriteData), .en(r9), .clk(clk), .Q(s0));  // open: clr
  Register #(.width(32)) register_4 (.D(WriteData), .en(r13), .clk(clk), .Q(o13));  // open: clr
  Register #(.width(32)) register_5 (.D(WriteData), .en(r17), .clk(clk), .Q(o17));  // open: clr
  Register #(.width(32)) register_6 (.D(WriteData), .en(r21), .clk(clk), .Q(o21));  // open: clr
  Register #(.width(32)) register_7 (.D(WriteData), .en(r25), .clk(clk), .Q(o25));  // open: clr
  Register #(.width(32)) register_8 (.D(WriteData), .en(r29), .clk(clk), .Q(o29));  // open: clr
  Demultiplexer #(.select(5)) demultiplexer_1 (
    .out0(r1), .out1(r2), .out2(r3), .out3(r4), .out4(r5), .out5(r6), .out6(r7), .out7(r8), .out8(r9),
    .out9(r10), .out10(r11), .out11(r12), .out12(r13), .out13(r14), .out14(r15), .out15(r16), .out16(r17),
    .out17(r18), .out18(r19), .out19(r20), .out20(r21), .out21(r22), .out22(r23), .out23(r24), .out24(r25),
    .out25(r26), .out26(r27), .out27(r28), .out28(r29), .out29(r30), .out30(r31), .out31(r32), .in(RegWEn),
    .sel(WriteIndex));
  Register #(.width(32)) register_9 (.D(WriteData), .en(r2), .clk(clk), .Q(ra));  // open: clr
  Register #(.width(32)) register_10 (.D(WriteData), .en(r6), .clk(clk), .Q(t0));  // open: clr
  Register #(.width(32)) register_11 (.D(WriteData), .en(r10), .clk(clk), .Q(s1));  // open: clr
  Register #(.width(32)) register_12 (.D(WriteData), .en(r14), .clk(clk), .Q(o14));  // open: clr
  Register #(.width(32)) register_13 (.D(WriteData), .en(r18), .clk(clk), .Q(o18));  // open: clr
  Register #(.width(32)) register_14 (.D(WriteData), .en(r22), .clk(clk), .Q(o22));  // open: clr
  Register #(.width(32)) register_15 (.D(WriteData), .en(r26), .clk(clk), .Q(o26));  // open: clr
  Register #(.width(32)) register_16 (.D(WriteData), .en(r30), .clk(clk), .Q(o30));  // open: clr
  Multiplexer #(.select(5), .width(32)) multiplexer_1 (
    .in0(o1), .in1(ra), .in2(sp), .in3(o4), .in4(o5), .in5(t0), .in6(t1), .in7(t2), .in8(s0), .in9(s1),
    .in10(a0), .in11(o12), .in12(o13), .in13(o14), .in14(o15), .in15(o16), .in16(o17), .in17(o18),
    .in18(o19), .in19(o20), .in20(o21), .in21(o22), .in22(o23), .in23(o24), .in24(o25), .in25(o26),
    .in26(o27), .in27(o28), .in28(o29), .in29(o30), .in30(o31), .in31(o32), .out(ReadData1), .sel(ReadIndex1));
  Register #(.width(32)) register_17 (.D(WriteData), .en(r3), .clk(clk), .Q(sp));  // open: clr
  Register #(.width(32)) register_18 (.D(WriteData), .en(r7), .clk(clk), .Q(t1));  // open: clr
  Register #(.width(32)) register_19 (.D(WriteData), .en(r11), .clk(clk), .Q(a0));  // open: clr
  Register #(.width(32)) register_20 (.D(WriteData), .en(r15), .clk(clk), .Q(o15));  // open: clr
  Register #(.width(32)) register_21 (.D(WriteData), .en(r19), .clk(clk), .Q(o19));  // open: clr
  Register #(.width(32)) register_22 (.D(WriteData), .en(r23), .clk(clk), .Q(o23));  // open: clr
  Register #(.width(32)) register_23 (.D(WriteData), .en(r27), .clk(clk), .Q(o27));  // open: clr
  Register #(.width(32)) register_24 (.D(WriteData), .en(r31), .clk(clk), .Q(o31));  // open: clr
  Multiplexer #(.select(5), .width(32)) multiplexer_2 (
    .in0(o1), .in1(ra), .in2(sp), .in3(o4), .in4(o5), .in5(t0), .in6(t1), .in7(t2), .in8(s0), .in9(s1),
    .in10(a0), .in11(o12), .in12(o13), .in13(o14), .in14(o15), .in15(o16), .in16(o17), .in17(o18),
    .in18(o19), .in19(o20), .in20(o21), .in21(o22), .in22(o23), .in23(o24), .in24(o25), .in25(o26),
    .in26(o27), .in27(o28), .in28(o29), .in29(o30), .in30(o31), .in31(o32), .out(ReadData2), .sel(ReadIndex2));
  Register #(.width(32)) register_25 (.D(WriteData), .en(r4), .clk(clk), .Q(o4));  // open: clr
  Register #(.width(32)) register_26 (.D(WriteData), .en(r8), .clk(clk), .Q(t2));  // open: clr
  Register #(.width(32)) register_27 (.D(WriteData), .en(r12), .clk(clk), .Q(o12));  // open: clr
  Register #(.width(32)) register_28 (.D(WriteData), .en(r16), .clk(clk), .Q(o16));  // open: clr
  Register #(.width(32)) register_29 (.D(WriteData), .en(r20), .clk(clk), .Q(o20));  // open: clr
  Register #(.width(32)) register_30 (.D(WriteData), .en(r24), .clk(clk), .Q(o24));  // open: clr
  Register #(.width(32)) register_31 (.D(WriteData), .en(r28), .clk(clk), .Q(o28));  // open: clr
  Register #(.width(32)) register_32 (.D(WriteData), .en(r32), .clk(clk), .Q(o32));  // open: clr

  // Other names for the same wires on the sheet: o2[31:0] = ra; o3[31:0] = sp; o6[31:0] = t0; o7[31:0] = t1;
  //   o8[31:0] = t2; o9[31:0] = s0; o10[31:0] = s1; o11[31:0] = a0

  // Notes on the sheet:
  //   INPUTS to your circuit
  //   DON'T CHANGE THE LOCATIONS OF THE INPUTS AND OUTPUTS!
  //   These are DEBUG/TEST outputs from your circuit.
  //   OUTPUTS from your circuit
endmodule
